// Logisim project CalOX_ALU.circ as structural Verilog: 8 circuits, main circuit ALU
module ALU (
  input  [7:0] input_A,
  input  [7:0] input_B,
  input  [7:0] instruction,
  output [7:0] output_8bits,
  output flag_0,
  output flag_overflow,
  output flag_negative,
  output bool_result
);

  wire and_1_out, decoder_1_out0, decoder_1_out1, decoder_1_out3, nand_1_out;
  wire [0:0] controlled_buffer_1_out;
  wire [1:0] controlled_buffer_1_out_2;
  wire [2:0] buffer_1_out;
  wire [7:0] calox_8bit_addernp_1_output_8bits;
  wire [7:3] buffer_1_out_2;

  assign {buffer_1_out_2, buffer_1_out} = input_B;  // Buffer buffer_1, 8 bits wide
  and and_1 (and_1_out, instruction[6], nand_1_out);
  nand nand_1 (nand_1_out, instruction[6], instruction[7]);
  Decoder #(.select(3)) decoder_1 (
    .out0(decoder_1_out0), .out1(decoder_1_out1), .out3(decoder_1_out3), .sel(instruction[2:0]),
    .en(and_1_out));  // open: out2, out4, out5, out6, out7
  assign {controlled_buffer_1_out_2, controlled_buffer_1_out[0]} = and_1_out ? instruction[5:3] : 3'bz;  // Controlled_Buffer controlled_buffer_1
  CalOX_8bit_AdderNP calox_8bit_addernp_1 (
    .input_A(input_A), .input_B({buffer_1_out_2, buffer_1_out}), .neg_inB(instruction[3]),
    .input_enable(decoder_1_out0), .output_8bits(calox_8bit_addernp_1_output_8bits),
    .negative_value(flag_negative), .zero_value(flag_0), .overflow(flag_overflow));
  CalOX_logic_instructor calox_logic_instructor_1 (
    .input_A(input_A), .input_B({buffer_1_out_2, buffer_1_out}), .enable_output(decoder_1_out1),
    .instruction_3bit({controlled_buffer_1_out_2, controlled_buffer_1_out[0]}),
    .output_8bit(calox_8bit_addernp_1_output_8bits));
  CalOX_condition_instructor calox_condition_instructor_1 (
    .output_enable(1'b1), .instruction_3bit({controlled_buffer_1_out_2, controlled_buffer_1_out[0]}),
    .input_A(input_A), .input_B({buffer_1_out_2, buffer_1_out}), .output_1bit(bool_result));
  CalOX_Shifter calox_shifter_1 (
    .input_A(input_A), .shift_amount(buffer_1_out), .enable_output(decoder_1_out3),
    .instruction(controlled_buffer_1_out_2), .output_8bit(calox_8bit_addernp_1_output_8bits));
  assign output_8bits = and_1_out ? calox_8bit_addernp_1_output_8bits : 8'bz;  // Controlled_Buffer controlled_buffer_2
endmodule

module CalOX_8bit_AdderNP (
  input  [7:0] input_A,
  input  neg_inB,
  input  [7:0] input_B,
  input  input_enable,
  output overflow,
  output zero_value,
  output [7:0] output_8bits,
  output negative_value
);

  wire adder_1_cout, and_1_out, not_1_out, or_1_out, xor_1_out, xor_2_out;
  wire [7:0] adder_1_out, calox_8bit_signnegator_1_output_8bits, calox_8bit_swc_1_output_8bits;

  CalOX_8bit_SignNegator calox_8bit_signnegator_1 (
    .input_8bits(input_B), .output_8bits(calox_8bit_signnegator_1_output_8bits));
  CalOX_8bit_SWC calox_8bit_swc_1 (
    .Input_A(input_B), .Input_B(calox_8bit_signnegator_1_output_8bits), .Input_selector(neg_inB),
    .output_8Bits(calox_8bit_swc_1_output_8bits));
  Adder adder_1 (.a(input_A), .b(calox_8bit_swc_1_output_8bits), .out(adder_1_out), .cout(adder_1_cout));  // open: cin
  xor xor_1 (xor_1_out, calox_8bit_swc_1_output_8bits[7], input_A[7]);
  not not_1 (not_1_out, xor_1_out);
  assign output_8bits = input_enable ? adder_1_out : 8'bz;  // Controlled_Buffer controlled_buffer_1
  and and_1 (and_1_out, calox_8bit_swc_1_output_8bits[7], input_A[7]);
  xor xor_2 (xor_2_out, and_1_out, adder_1_out[7]);
  CalOX_8bit_zeroDetector calox_8bit_zerodetector_1 (.input_8bits(adder_1_out), .output_8bits(zero_value));
  and and_2 (negative_value, adder_1_out[7], xor_1_out);
  or or_1 (or_1_out, not_1_out, xor_2_out);
  and and_3 (overflow, or_1_out, adder_1_cout);
endmodule

module CalOX_8bit_SWC (
  input  [7:0] Input_A,
  input  [7:0] Input_B,
  input  Input_selector,
  output [7:0] output_8Bits
);

  wire not_1_out;

  assign output_8Bits = not_1_out ? Input_A : 8'bz;  // Controlled_Buffer controlled_buffer_1
  not not_1 (not_1_out, Input_selector);
  assign output_8Bits = Input_selector ? Input_B : 8'bz;  // Controlled_Buffer controlled_buffer_2
endmodule

module CalOX_8bit_SignNegator (
  input  [7:0] input_8bits,
  output [7:0] output_8bits
);

  wire [7:0] not_1_out;

  assign not_1_out = ~input_8bits;  // NOT_Gate not_1, 8 bits wide
  Adder adder_1 (.a(not_1_out), .b(8'h1), .out(output_8bits));  // open: cin, cout
endmodule

module CalOX_8bit_zeroDetector (
  input  [7:0] input_8bits,
  output output_8bits
);

  nor nor_1 (output_8bits, input_8bits[0], input_8bits[1], input_8bits[2], input_8bits[3], input_8bits[4], input_8bits[5], input_8bits[6], input_8bits[7]);
endmodule

module CalOX_condition_instructor (
  input  [7:0] input_A,
  input  [7:0] input_B,
  input  output_enable,
  input  [2:0] instruction_3bit,
  output output_1bit
);

  wire comparator_1_eq, comparator_1_gt, comparator_1_lt, decoder_1_out0, decoder_1_out1, decoder_1_out2,
       decoder_1_out3, decoder_1_out4, decoder_1_out5, or_1_out;
  wire [7:0] calox_8bit_swc_1_output_8bits;

  CalOX_8bit_SWC calox_8bit_swc_1 (
    .Input_A({8{1'b0}}), .Input_B(input_B), .Input_selector(or_1_out),
    .output_8Bits(calox_8bit_swc_1_output_8bits));
  Decoder #(.select(3)) decoder_1 (
    .out0(decoder_1_out0), .out1(decoder_1_out1), .out2(decoder_1_out2), .out3(decoder_1_out3),
    .out4(decoder_1_out4), .out5(decoder_1_out5), .sel(instruction_3bit), .en(output_enable));  // open: out6, out7
  or or_1 (or_1_out, decoder_1_out3, decoder_1_out4, decoder_1_out5);
  Comparator comparator_1 (
    .a(input_A), .b(calox_8bit_swc_1_output_8bits), .gt(comparator_1_gt), .eq(comparator_1_eq),
    .lt(comparator_1_lt));
  assign output_1bit = decoder_1_out0 ? comparator_1_lt : 1'bz;  // Controlled_Buffer controlled_buffer_1
  assign output_1bit = decoder_1_out1 ? comparator_1_eq : 1'bz;  // Controlled_Buffer controlled_buffer_2
  assign output_1bit = decoder_1_out2 ? comparator_1_gt : 1'bz;  // Controlled_Buffer controlled_buffer_3
  assign output_1bit = decoder_1_out3 ? comparator_1_lt : 1'bz;  // Controlled_Buffer controlled_buffer_4
  assign output_1bit = decoder_1_out4 ? comparator_1_gt : 1'bz;  // Controlled_Buffer controlled_buffer_5
  assign output_1bit = decoder_1_out5 ? comparator_1_lt : 1'bz;  // Controlled_Buffer controlled_buffer_6
endmodule

module CalOX_logic_instructor (
  input  [7:0] input_A,
  input  [7:0] input_B,
  input  enable_output,
  input  [2:0] instruction_3bit,
  output [7:0] output_8bit
);

  wire decoder_1_out0, decoder_1_out1, decoder_1_out2, decoder_1_out3, decoder_1_out4, decoder_1_out5,
       or_2_out, or_3_out, or_4_out;
  wire [7:0] and_1_out, multiplexer_1_out, multiplexer_2_out, multiplexer_3_out, not_1_out, not_2_out,
       not_3_out, or_1_out, xor_1_out;

  assign and_1_out = input_A & input_B;  // AND_Gate and_1, 8 bits wide
  assign or_1_out = input_A | input_B;  // OR_Gate or_1, 8 bits wide
  assign xor_1_out = input_A ^ input_B;  // XOR_Gate xor_1, 8 bits wide
  assign not_1_out = ~and_1_out;  // NOT_Gate not_1, 8 bits wide
  assign not_2_out = ~or_1_out;  // NOT_Gate not_2, 8 bits wide
  assign not_3_out = ~xor_1_out;  // NOT_Gate not_3, 8 bits wide
  Multiplexer #(.width(8)) multiplexer_1 (
    .in0(and_1_out), .in1(not_1_out), .out(multiplexer_1_out), .sel(decoder_1_out1));
  Multiplexer #(.width(8)) multiplexer_2 (
    .in0(or_1_out), .in1(not_2_out), .out(multiplexer_2_out), .sel(decoder_1_out3));
  Multiplexer #(.width(8)) multiplexer_3 (
    .in0(xor_1_out), .in1(not_3_out), .out(multiplexer_3_out), .sel(decoder_1_out5));
  Decoder #(.select(3)) decoder_1 (
    .out0(decoder_1_out0), .out1(decoder_1_out1), .out2(decoder_1_out2), .out3(decoder_1_out3),
    .out4(decoder_1_out4), .out5(decoder_1_out5), .sel(instruction_3bit), .en(enable_output));  // open: out6, out7
  or or_2 (or_2_out, decoder_1_out0, decoder_1_out1);
  or or_3 (or_3_out, decoder_1_out2, decoder_1_out3);
  or or_4 (or_4_out, decoder_1_out4, decoder_1_out5);
  assign output_8bit = or_2_out ? multiplexer_1_out : 8'bz;  // Controlled_Buffer controlled_buffer_1
  assign output_8bit = or_3_out ? multiplexer_2_out : 8'bz;  // Controlled_Buffer controlled_buffer_2
  assign output_8bit = or_4_out ? multiplexer_3_out : 8'bz;  // Controlled_Buffer controlled_buffer_3
endmodule

module CalOX_Shifter (
  input  [7:0] input_A,
  input  [2:0] shift_amount,
  input  enable_output,
  input  [1:0] instruction,
  output [7:0] output_8bit
);

  wire decoder_1_out0, decoder_1_out1, decoder_1_out2, decoder_1_out3;
  wire [7:0] shifter_1_out, shifter_2_out, shifter_3_out, shifter_4_out;

  Shifter shifter_1 (.in(input_A), .\dist (shift_amount), .out(shifter_1_out));
  Shifter #(.shift("lr")) shifter_2 (.in(input_A), .\dist (shift_amount), .out(shifter_2_out));
  Shifter #(.shift("rl")) shifter_3 (.in(input_A), .\dist (shift_amount), .out(shifter_3_out));
  Shifter #(.shift("rr")) shifter_4 (.in(input_A), .\dist (shift_amount), .out(shifter_4_out));
  Decoder #(.select(2)) decoder_1 (
    .out0(decoder_1_out0), .out1(decoder_1_out1), .out2(decoder_1_out2), .out3(decoder_1_out3),
    .sel(instruction), .en(enable_output));
  assign output_8bit = decoder_1_out0 ? shifter_1_out : 8'bz;  // Controlled_Buffer controlled_buffer_1
  assign output_8bit = decoder_1_out1 ? shifter_2_out : 8'bz;  // Controlled_Buffer controlled_buffer_2
  assign output_8bit = decoder_1_out2 ? shifter_3_out : 8'bz;  // Controlled_Buffer controlled_buffer_3
  assign output_8bit = decoder_1_out3 ? shifter_4_out : 8'bz;  // Controlled_Buffer controlled_buffer_4
endmodule
