// Logisim project CalOX_CPU.circ as structural Verilog: 4 circuits, main circuit CPU
module CPU (
  input  [7:0] in_1,
  input  [7:0] in_2,
  input  [7:0] in_3,
  output [7:0] out_4,
  output [7:0] out_5
);

  wire and_1_out, buffer_1_out, buffer_2_out, clock_1_out, decoder_1_out1, decoder_1_out2, decoder_2_out0,
       decoder_2_out1, decoder_2_out2, decoder_2_out3, decoder_2_out4, decoder_2_out5, decoder_2_out6,
       decoder_2_out7, decoder_2_out8, decoder_2_out9, decoder_2_out10, decoder_2_out15, decoder_3_out0,
       decoder_3_out1, decoder_3_out2, decoder_3_out3, decoder_3_out4, decoder_3_out5, decoder_3_out6,
       decoder_3_out7, decoder_3_out8, decoder_3_out9, decoder_3_out10, decoder_3_out15,
       demultiplexer_1_out0, demultiplexer_1_out1, or_1_out, or_2_out, or_3_out, or_4_out;
  wire [7:0] alu_1_p6, buffer_3_out, buffer_4_out, buffer_5_out, buffer_8_out, buffer_9_out, buffer_10_out,
       buffer_13_out, buffer_14_out, buffer_18_out, buffer_19_out, calox_reg_1_always_output,
       calox_reg_1_data_output, calox_reg_2_always_output, calox_reg_2_data_output,
       calox_reg_3_always_output, calox_reg_3_data_output, calox_reg_4_always_output,
       calox_reg_4_data_output, calox_reg_5_always_output, calox_reg_5_data_output,
       calox_reg_6_always_output, calox_reg_6_data_output, calox_reg_7_always_output,
       calox_reg_7_data_output, calox_reg_8_always_output, calox_reg_8_data_output,
       calox_reg_9_always_output, calox_reg_9_data_output, calox_reg_10_always_output,
       calox_reg_10_data_output, calox_reg_11_always_output, calox_reg_11_data_output,
       calox_reg_12_always_output, calox_reg_12_data_output, calox_reg_13_always_output,
       calox_reg_13_data_output, controlled_buffer_1_out, controlled_buffer_2_out;
  wire [7:1] undriven;

  or or_1 (or_1_out, decoder_1_out2, decoder_1_out1);
  Decoder #(.select(2)) decoder_1 (
    .out1(decoder_1_out1), .out2(decoder_1_out2), .sel(in_3[7:6]));  // open: out0, out3, en
  Decoder #(.select(4)) decoder_2 (
    .out0(decoder_2_out0), .out1(decoder_2_out1), .out2(decoder_2_out2), .out3(decoder_2_out3),
    .out4(decoder_2_out4), .out5(decoder_2_out5), .out6(decoder_2_out6), .out7(decoder_2_out7),
    .out8(decoder_2_out8), .out9(decoder_2_out9), .out10(decoder_2_out10), .out15(decoder_2_out15),
    .sel(in_1[3:0]), .en(decoder_1_out2));  // open: out11, out12, out13, out14
  Decoder #(.select(4)) decoder_3 (
    .out0(decoder_3_out0), .out1(decoder_3_out1), .out2(decoder_3_out2), .out3(decoder_3_out3),
    .out4(decoder_3_out4), .out5(decoder_3_out5), .out6(decoder_3_out6), .out7(decoder_3_out7),
    .out8(decoder_3_out8), .out9(decoder_3_out9), .out10(decoder_3_out10), .out15(decoder_3_out15),
    .sel(in_1[7:4]), .en(or_1_out));  // open: out11, out12, out13, out14
  or or_2 (or_2_out, in_1[4], in_1[5], in_1[6], in_1[7]);
  Clock clock_1 (.out(clock_1_out));
  and and_1 (and_1_out, or_2_out, decoder_1_out1);
  Demultiplexer demultiplexer_1 (
    .out0(demultiplexer_1_out0), .out1(demultiplexer_1_out1), .in(and_1_out), .sel(in_1[0]));
  assign controlled_buffer_1_out = decoder_3_out0 ? in_2 : 8'bz;  // Controlled_Buffer controlled_buffer_1
  buf buffer_1 (buffer_1_out, decoder_2_out9);
  or or_3 (or_3_out, demultiplexer_1_out0, buffer_1_out);
  buf buffer_2 (buffer_2_out, decoder_2_out10);
  or or_4 (or_4_out, demultiplexer_1_out1, buffer_2_out);
  assign buffer_3_out = controlled_buffer_1_out;  // Buffer buffer_3, 8 bits wide
  assign buffer_4_out = controlled_buffer_1_out;  // Buffer buffer_4, 8 bits wide
  assign buffer_5_out = controlled_buffer_1_out;  // Buffer buffer_5, 8 bits wide
  assign controlled_buffer_1_out = calox_reg_1_data_output;  // Buffer buffer_6, 8 bits wide
  CalOX_reg calox_reg_1 (
    .data_input(buffer_3_out), .write_enable(decoder_2_out1), .CK(clock_1_out), .load_enable(decoder_3_out1),
    .data_output(calox_reg_1_data_output), .always_output(calox_reg_1_always_output));  // open: reset_value
  assign controlled_buffer_1_out = calox_reg_2_data_output;  // Buffer buffer_7, 8 bits wide
  CalOX_reg calox_reg_2 (
    .data_input(buffer_4_out), .write_enable(decoder_2_out5), .CK(clock_1_out), .load_enable(decoder_3_out5),
    .data_output(calox_reg_2_data_output), .always_output(calox_reg_2_always_output));  // open: reset_value
  CalOX_reg calox_reg_3 (
    .data_input(buffer_5_out), .write_enable(or_3_out), .CK(clock_1_out), .load_enable(1'b1),
    .data_output(calox_reg_3_data_output), .always_output(calox_reg_3_always_output));  // open: reset_value
  assign buffer_8_out = controlled_buffer_1_out;  // Buffer buffer_8, 8 bits wide
  assign buffer_9_out = controlled_buffer_1_out;  // Buffer buffer_9, 8 bits wide
  assign buffer_10_out = controlled_buffer_1_out;  // Buffer buffer_10, 8 bits wide
  CalOX_reg calox_reg_4 (
    .data_input(buffer_10_out), .write_enable(or_4_out), .CK(clock_1_out), .load_enable(1'b1),
    .data_output(calox_reg_4_data_output), .always_output(calox_reg_4_always_output));  // open: reset_value
  assign controlled_buffer_1_out = calox_reg_5_data_output;  // Buffer buffer_11, 8 bits wide
  CalOX_reg calox_reg_5 (
    .data_input(buffer_8_out), .write_enable(decoder_2_out2), .CK(clock_1_out), .load_enable(decoder_3_out2),
    .data_output(calox_reg_5_data_output), .always_output(calox_reg_5_always_output));  // open: reset_value
  assign controlled_buffer_1_out = calox_reg_6_data_output;  // Buffer buffer_12, 8 bits wide
  CalOX_reg calox_reg_6 (
    .data_input(buffer_9_out), .write_enable(decoder_2_out6), .CK(clock_1_out), .load_enable(decoder_3_out6),
    .data_output(calox_reg_6_data_output), .always_output(calox_reg_6_always_output));  // open: reset_value
  // ALU alu_1: pin names not known; wires that end beside it: calox_reg_3_always_output, calox_reg_4_always_output, calox_reg_3_data_output, calox_reg_4_data_output, in_3, alu_1_p6
  assign buffer_13_out = controlled_buffer_1_out;  // Buffer buffer_13, 8 bits wide
  assign buffer_14_out = controlled_buffer_1_out;  // Buffer buffer_14, 8 bits wide
  assign controlled_buffer_1_out = calox_reg_7_data_output;  // Buffer buffer_15, 8 bits wide
  CalOX_reg calox_reg_7 (
    .data_input(alu_1_p6), .write_enable(1'b1), .CK(clock_1_out), .load_enable(decoder_3_out9),
    .data_output(calox_reg_7_data_output), .always_output(calox_reg_7_always_output));  // open: reset_value
  assign controlled_buffer_1_out = calox_reg_8_data_output;  // Buffer buffer_16, 8 bits wide
  CalOX_reg calox_reg_8 (
    .data_input(buffer_13_out), .write_enable(decoder_2_out3), .CK(clock_1_out),
    .load_enable(decoder_3_out3), .data_output(calox_reg_8_data_output),
    .always_output(calox_reg_8_always_output));  // open: reset_value
  assign controlled_buffer_1_out = calox_reg_9_data_output;  // Buffer buffer_17, 8 bits wide
  CalOX_reg calox_reg_9 (
    .data_input(buffer_14_out), .write_enable(decoder_2_out7), .CK(clock_1_out),
    .load_enable(decoder_3_out7), .data_output(calox_reg_9_data_output),
    .always_output(calox_reg_9_always_output));  // open: reset_value
  CalOX_reg calox_reg_10 (
    .CK(clock_1_out), .load_enable(decoder_3_out10), .data_output(calox_reg_10_data_output),
    .always_output(calox_reg_10_always_output));  // open: data_input, write_enable, reset_value
  assign buffer_18_out = controlled_buffer_1_out;  // Buffer buffer_18, 8 bits wide
  assign buffer_19_out = controlled_buffer_1_out;  // Buffer buffer_19, 8 bits wide
  assign controlled_buffer_1_out = calox_reg_10_data_output;  // Buffer buffer_20, 8 bits wide
  assign controlled_buffer_1_out = calox_reg_11_data_output;  // Buffer buffer_21, 8 bits wide
  CalOX_reg calox_reg_11 (
    .data_input(buffer_18_out), .write_enable(decoder_2_out4), .CK(clock_1_out),
    .load_enable(decoder_3_out4), .data_output(calox_reg_11_data_output),
    .always_output(calox_reg_11_always_output));  // open: reset_value
  assign controlled_buffer_1_out = calox_reg_12_data_output;  // Buffer buffer_22, 8 bits wide
  CalOX_reg calox_reg_12 (
    .data_input(buffer_19_out), .write_enable(decoder_2_out8), .CK(clock_1_out),
    .load_enable(decoder_3_out8), .data_output(calox_reg_12_data_output),
    .always_output(calox_reg_12_always_output));  // open: reset_value
  CalOX_reg calox_reg_13 (
    .data_input({undriven, 1'b1}), .write_enable(1'b1), .CK(clock_1_out), .load_enable(1'b1),
    .data_output(calox_reg_13_data_output), .always_output(calox_reg_13_always_output));  // open: reset_value
  assign controlled_buffer_2_out = decoder_2_out15 ? controlled_buffer_1_out : 8'bz;  // Controlled_Buffer controlled_buffer_2
  CalOX_counter calox_counter_1 (
    .clock_0(clock_1_out), .step_0(calox_reg_13_data_output), .set_value(controlled_buffer_2_out),
    .output_8bit(out_5));  // open: enable_set_value
  assign controlled_buffer_1_out = decoder_3_out15 ? out_5 : 8'bz;  // Controlled_Buffer controlled_buffer_3
  assign out_4 = decoder_2_out0 ? controlled_buffer_1_out : 8'bz;  // Controlled_Buffer controlled_buffer_4

  // Notes on the sheet:
  //   move value to ->
  //   move value from <-
endmodule

module CalOX_counter (
  input  [7:0] set_value,
  input  enable_set_value,
  input  [7:0] step_0,
  input  clock_0,
  output [7:0] output_8bit
);

  wire not_1_out;
  wire [7:0] adder_1_out, controlled_buffer_1_out;

  Adder adder_1 (.a(step_0), .b(output_8bit), .out(adder_1_out));  // open: cin, cout
  assign controlled_buffer_1_out = enable_set_value ? set_value : 8'bz;  // Controlled_Buffer controlled_buffer_1
  Register register_1 (.D(controlled_buffer_1_out), .en(clock_0), .clk(clock_0), .Q(output_8bit));  // open: clr
  assign controlled_buffer_1_out = not_1_out ? adder_1_out : 8'bz;  // Controlled_Buffer controlled_buffer_2
  not not_1 (not_1_out, enable_set_value);
endmodule

module CalOX_reg (
  input  [7:0] data_input,
  input  load_enable,
  input  write_enable,
  input  CK,
  input  reset_value,
  output [7:0] data_output,
  output [7:0] always_output
);

  Register register_1 (.D(data_input), .en(write_enable), .clk(CK), .Q(always_output), .clr(reset_value));
  assign data_output = load_enable ? always_output : 8'bz;  // Controlled_Buffer controlled_buffer_1
endmodule

module CalOX_instruction_decoder (
  input  [7:0] instruction_input,
  output [7:0] instruction_output,
  output out_3,
  output out_4,
  output out_5,
  output out_6
);

  Decoder #(.select(2)) decoder_1 (
    .out0(out_3), .out1(out_4), .out2(out_5), .out3(out_6), .sel(instruction_input[7:6]));  // open: en

  assign instruction_output = instruction_input;
endmodule
